// Logisim project cpu.circ as structural Verilog: 1 circuit, main circuit main
module main (
  input  [31:0] RS_READ_VALUE,
  input  [31:0] RT_READ_VALUE,
  input  [31:0] INSTRUCTION,
  input  CLOCK,
  input  RESET,
  output [31:0] Lo,
  output [31:0] Hi,
  output [31:0] t0,
  output [31:0] t1,
  output [31:0] t2,
  output [31:0] t3,
  output [4:0] RS,
  output [4:0] RT,
  output [4:0] Write_Register,
  output [31:0] RD_WRITE_VALUE,
  output RD_WRITE_ENABLE,
  output [23:0] FETCH_ADDRESS
);

  // regfile_main RegFile: pin names not known
  // alu_main ALU: pin names not known
  // mem_main MEM: pin names not known

  // Other names for the same wires on the sheet: clk = CLOCK; RS_VAL[31:0] = RS_READ_VALUE; rst = RESET;
  //   RT_VAL[31:0] = RT_READ_VALUE

  // Notes on the sheet:
  //   These are outputs/inputs from run.circ
  //   These are outputs to run.circ
  //   Feel free to move these
endmodule
